# Fritzing sketch RC Arm Tank (saved by Fritzing 0.9.4)
perfboards: 2

parts:
  IC1 = L293D [package=THT]
  Part1 = Arduino Uno (Rev3)
  M2 = DC Motor
  Part2 = Bluetooth HC-05 Macho
  M1 = DC Motor
  J2 = female pin header, 1 pin [form="♀ (female)"]
  J3 = female pin header, 1 pin [form="♀ (female)"]
  J4 = female pin header, 1 pin [form="♀ (female)"]
  J5 = female pin header, 1 pin [form="♀ (female)"]
  J6 = Screw terminal - 2 pins [package=THT]
  J7 = Screw terminal - 2 pins [package=THT]
  J9 = female pin header, 1 pin [form="♀ (female)"]  # not connected
  J10 = female pin header, 1 pin [form="♀ (female)"]
  Part3 = Arduino Nano (Rev3.0) (ICSP)
  J11 = female pin header, 3 pins [form="♀ (female)"]
  J12 = female pin header, 3 pins [form="♀ (female)"]
  J13 = female pin header, 3 pins [form="♀ (female)"]
  J14 = female pin header, 3 pins [form="♀ (female)"]
  J15 = female pin header, 3 pins [form="♀ (female)"]
  J16 = female pin header, 3 pins [form="♀ (female)"]
  M3 = RioRand LM2596
  J17 = Basic Servo
  J18 = Basic Servo
  J19 = Basic Servo
  J22 = Basic Servo
  J23 = female pin header, 15 pins [form="♀ (female)"]
  J24 = female pin header, 15 pins [form="♀ (female)"]
  U1 = LIPO-1000mAh [package=lipo-1000]
  J21 = Basic Servo
  J20 = Basic Servo

nets:
  N1: IC1.Enable_1, IC1.+V
  N2: IC1.In_1, Part1.D6_PWM
  GND: IC1.0V, Part1.GND, Part2.GND, J7.pin2, U1.-
  N3: IC1.In_2, Part1.D11_PWM/MOSI
  N4: IC1.In_3, Part1.D5_PWM
  N5: IC1.Out_3_(_Controlled_by_Enable_2_), M1.pin_2, J4.pin1
  N6: IC1.In_4, Part1.D3_PWM
  N7: Part1.D2, Part2.TXD
  N8: Part1.D4, Part2.RXD
  N9: Part1.VIN, J6.pin1, U1.+
  N10: M2.pin_1, J3.pin1
  N11: M2.pin_2, J2.pin1
  N12: M1.pin_1, J5.pin1
  N13: J6.pin2, M3.Pin_1
  N14: J10.pin1, M3.Pin_2
  N15: Part3.D1/TX, J23.pin15
  N16: Part3.D0/RX, J23.pin14
  N17: Part3.RESET, J23.pin13, J24.pin13
  N18: Part3.GND, J23.pin12, J24.pin14
  N19: Part3.D2, J23.pin11
  N20: Part3.D3, J23.pin10
  N21: Part3.D4, J23.pin9
  N22: Part3.D5, J23.pin8
  N23: Part3.D6, J23.pin7
  N24: Part3.D7, J23.pin6
  N25: Part3.D8, J23.pin5
  N26: Part3.D9, J23.pin4
  N27: Part3.D10, J23.pin3
  N28: Part3.D11/MOSI, J23.pin2
  N29: Part3.D12/MISO, J23.pin1
  N30: Part3.VIN, J24.pin15
  N31: Part3.5V, J24.pin12
  N32: Part3.A7, J24.pin11
  N33: Part3.A6, J24.pin10
  N34: Part3.A5, J24.pin9
  N35: Part3.A4, J24.pin8
  N36: Part3.A3, J24.pin7
  N37: Part3.A2, J24.pin6
  N38: Part3.A1, J24.pin5
  N39: Part3.A0, J24.pin4
  N40: Part3.AREF, J24.pin3
  N41: Part3.3V3, J24.pin2
  N42: Part3.D13/SCK, J24.pin1
  GND_2: J11.pin1, J14.pin1, M3.Pin_4, J17.gnd, J20.gnd
  VCC: J11.pin2, J14.pin2, M3.Pin_3, J17.vcc, J20.vcc
  N43: J11.pin3, J17.pulse
  GND_3: J12.pin1, J15.pin3, J18.gnd, J21.gnd
  N44: J12.pin2, J18.vcc
  N45: J12.pin3, J18.pulse
  N46: J13.pin1, J19.gnd
  N47: J13.pin2, J19.vcc
  N48: J13.pin3, J19.pulse
  N49: J14.pin3, J20.pulse
  N50: J15.pin1, J21.pulse
  N51: J15.pin2, J21.vcc
  N52: J16.pin1, J22.pulse
  N53: J16.pin2, J22.vcc
  N54: J16.pin3, J22.gnd
