# Fritzing sketch RC Nerf Turret Tank (saved by Fritzing 0.9.4)
perfboards: 2

parts:
  Part4 = Arduino Uno (Rev3)
  U2 = LIPO-1000mAh [package=lipo-1000]
  Part5 = Bluetooth HC-05 Macho
  J25 = female pin header, 1 pin [form="♀ (female)"]
  J26 = female pin header, 1 pin [form="♀ (female)"]
  J27 = female pin header, 1 pin [form="♀ (female)"]
  J28 = female pin header, 1 pin [form="♀ (female)"]
  J29 = female pin header, 1 pin [form="♀ (female)"]  # not connected
  J30 = female pin header, 1 pin [form="♀ (female)"]
  J31 = Screw terminal - 2 pins [package=THT]
  J32 = Screw terminal - 2 pins [package=THT]
  IC2 = L293D [package=THT]
  M4 = DC Motor
  M5 = DC Motor
  J33 = female pin header, 3 pins [form="♀ (female)"]
  J34 = female pin header, 3 pins [form="♀ (female)"]
  J35 = female pin header, 3 pins [form="♀ (female)"]
  M6 = RioRand LM2596
  J36 = Basic Servo
  J37 = Basic Servo
  J38 = Basic Servo
  J39 = female pin header, 15 pins [form="♀ (female)"]
  J40 = female pin header, 15 pins [form="♀ (female)"]
  Part6 = Arduino Nano (Rev3.0) (ICSP)
  M7 = DC Motor
  Q1 = NPN-Transistor [package="SOT-23 [SMD]"]  # not connected
  D1 = Diode [package=diode-1n4001]  # not connected
  R1 = Resistor [tolerance=±5% resistance=220 package="0402 [SMD]"]  # not connected
  M8 = DC Motor

nets:
  N1: Part4.D11_PWM/MOSI, IC2.In_2
  GND: Part4.GND, U2.-, Part5.GND, J32.pin2, IC2.0V
  N2: Part4.D2, Part5.TXD
  N3: Part4.D3_PWM, IC2.In_4
  N4: Part4.D4, Part5.RXD
  N5: Part4.D5_PWM, IC2.In_3
  N6: Part4.D6_PWM, IC2.In_1
  N7: Part4.VIN, U2.+, J31.pin1
  N8: J25.pin1, M4.pin_1
  N9: J26.pin1, IC2.Out_3_(_Controlled_by_Enable_2_), M4.pin_2
  N10: J27.pin1, M5.pin_1
  N11: J28.pin1, M6.Pin_2
  N12: J30.pin1, M5.pin_2
  N13: J31.pin2, M6.Pin_1
  N14: IC2.Enable_1, IC2.+V
  GND_2: J33.pin1, J34.pin1, J35.pin1, M6.Pin_4, J36.gnd, J37.gnd, J38.gnd
  VCC: J33.pin2, J34.pin2, J35.pin2, M6.Pin_3, J36.vcc, J37.vcc, J38.vcc
  N15: J33.pin3, J36.pulse
  N16: J34.pin3, J38.pulse
  N17: J35.pin3, J37.pulse
  N18: J39.pin1, Part6.D12/MISO
  N19: J39.pin2, Part6.D11/MOSI
  N20: J39.pin3, Part6.D10
  N21: J39.pin4, Part6.D9
  N22: J39.pin5, Part6.D8
  N23: J39.pin6, Part6.D7
  N24: J39.pin7, Part6.D6
  N25: J39.pin8, Part6.D5
  N26: J39.pin9, Part6.D4
  N27: J39.pin10, Part6.D3
  N28: J39.pin11, Part6.D2
  N29: J39.pin12, J40.pin14, Part6.GND
  N30: J39.pin13, J40.pin13, Part6.RESET
  N31: J39.pin14, Part6.D0/RX
  N32: J39.pin15, Part6.D1/TX
  N33: J40.pin1, Part6.D13/SCK
  N34: J40.pin2, Part6.3V3
  N35: J40.pin3, Part6.AREF
  N36: J40.pin4, Part6.A0
  N37: J40.pin5, Part6.A1
  N38: J40.pin6, Part6.A2
  N39: J40.pin7, Part6.A3
  N40: J40.pin8, Part6.A4
  N41: J40.pin9, Part6.A5
  N42: J40.pin10, Part6.A6
  N43: J40.pin11, Part6.A7
  N44: J40.pin12, Part6.5V
  N45: J40.pin15, Part6.VIN
  N46: M7.pin_1, M8.pin_2
  N47: M7.pin_2, M8.pin_1
