# Fritzing sketch RC Sherman Tank (saved by Fritzing 0.9.4)
perfboards: 2

parts:
  IC1 = L293D [package=THT]
  Part1 = Arduino Uno (Rev3)
  M2 = DC Motor
  LED1 = LEDs [package=led10mm]
  LED2 = LEDs [package=led10mm]
  LED3 = LEDs [package=led10mm]
  LED4 = LEDs [package=led10mm]
  S2 = Toggle Switch [package=THT]
  Part2 = Bluetooth HC-05 Macho
  J1 = Basic Servo
  M1 = DC Motor
  J2 = female pin header, 1 pin [form="♀ (female)"]
  J3 = female pin header, 1 pin [form="♀ (female)"]
  J4 = female pin header, 1 pin [form="♀ (female)"]
  J5 = female pin header, 1 pin [form="♀ (female)"]
  J6 = Screw terminal - 2 pins [package=THT]
  J7 = Screw terminal - 2 pins [package=THT]
  VCC2 = Battery
  VCC3 = Battery
  J8 = female pin header, 3 pins [form="♀ (female)"]
  J9 = female pin header, 1 pin [form="♀ (female)"]  # not connected
  J10 = female pin header, 1 pin [form="♀ (female)"]  # not connected
  R1 = Resistor [tolerance=±5% resistance=220 package=THT]
  R2 = Resistor [tolerance=±5% resistance=220 package=THT]
  R3 = Resistor [tolerance=±5% resistance=220 package=THT]
  R4 = Resistor [tolerance=±5% resistance=220 package=THT]
  C1 = Electrolytic Capacitor [capacitance=100µF voltage=16V package="100 mil [THT, electrolytic]"]  # not connected

nets:
  N1: IC1.Enable_1, IC1.+V
  N2: IC1.In_1, Part1.D9_PWM
  GND: IC1.0V, Part1.GND, Part2.GND
  N3: IC1.In_2, Part1.D10_PWM/SS
  N4: IC1.+Vmotor, Part1.VIN, J6.pin1, VCC2.+
  N5: IC1.In_3, Part1.D6_PWM
  N6: IC1.Out_3_(_Controlled_by_Enable_2_), M1.pin_2, J4.pin1
  N7: IC1.In_4, Part1.D5_PWM
  N8: Part1.D8, LED3.C
  N9: Part1.D12/MISO, LED2.C
  N10: Part1.D13/SCK, LED1.A
  N11: Part1.D0/RX, Part2.TXD
  N12: Part1.D1/TX, Part2.RXD
  N13: Part1.D7, LED4.A
  N14: M2.pin_1, J3.pin1
  N15: M2.pin_2, J2.pin1
  N16: LED1.C, R4.Pin_1
  N17: LED2.A, R3.Pin_1
  N18: LED3.A, R2.Pin_1
  N19: LED4.C, R1.Pin_1
  N20: S2.L1, J6.pin2, VCC2.-
  N21: S2.COM, J7.pin1, VCC3.+
  N22: J1.gnd, J8.pin1
  N23: J1.vcc, J8.pin2
  N24: J1.pulse, J8.pin3
  N25: M1.pin_1, J5.pin1
  N26: J7.pin2, VCC3.-
